# Fritzing sketch VM167Box (saved by Fritzing 1.0.3b)
circuit board: 12.5cm x 8.1cm
perfboards: 1

parts:
  J15 = female pin header, 2 pins [form="♀ (female)"]
  J11 = female pin header, 2 pins [form="♀ (female)"]
  R5 = Resistor [tolerance=±5% power=0.25W resistance=10k package=THT]
  J21 = female pin header, 2 pins [form="♀ (female)"]
  J10 = female pin header, 2 pins [form="♀ (female)"]
  J14 = female pin header, 2 pins [form="♀ (female)"]
  R1 = Resistor [tolerance=±5% power=0.25W resistance=100 package=THT]
  J19 = female pin header, 2 pins [form="♀ (female)"]
  C1 = Electrolytic Capacitor [capacitance=1µF voltage=35V package="100 mil [THT, electrolytic]"]
  Fuse1 = Fuse with Handler [part_number=Htc-15m]
  R6 = Resistor [tolerance=±5% power=0.25W resistance=10k package=THT]
  R4 = Resistor [tolerance=±5% power=0.25W resistance=100 package=THT]
  Q2 = npn-Powertransistor [package="TO220 [THT]"]
  R2 = Resistor [tolerance=±5% power=0.25W resistance=100 package=THT]
  J18 = female pin header, 2 pins [form="♀ (female)"]
  J7 = female pin header, 9 pins [form="♀ (female)"]
  J1 = male pin header, 8 pins [form="♂ (male)"]
  J17 = female pin header, 2 pins [form="♀ (female)"]
  J16 = female pin header, 2 pins [form="♀ (female)"]
  J9 = male pin header, 2 pins [form="♂ (male)"]
  Q1 = npn-Powertransistor [package="TO220 [THT]"]
  R6_2 = Resistor [tolerance=±5% power=0.25W resistance=10k package=THT]
  J6 = female pin header, 9 pins [form="♀ (female)"]
  R8 = Resistor [tolerance=±5% power=0.25W resistance=10k package=THT]
  J22 = female pin header, 2 pins [form="♀ (female)"]
  R3 = Resistor [tolerance=±5% power=0.25W resistance=100 package=THT]
  C2 = Electrolytic Capacitor [capacitance=1µF voltage=35V package="100 mil [THT, electrolytic]"]
  J5 = male pin header, 9 pins [form="♂ (male)"]
  J13 = female pin header, 2 pins [form="♀ (female)"]
  J2 = female pin header, 8 pins [form="♀ (female)"]
  J3 = female pin header, 8 pins [form="♀ (female)"]
  RCA1 = RCA [package=pth]
  RCA2 = RCA [package=pth]
  U2 = LM 358 Dual Op-Amp [package="DIP8 [THT]"]
  J4 = screw terminal, 8 pins
  J8 = screw terminal, 9 pins
  J12 = Screw terminal - 2 pins [package=THT]
  D4 = Diode [package=diode-1n4001]
  D6 = Diode [package=diode-1n4001]
  D8 = Diode [package=diode-1n4001]
  D1 = Diode [package=diode-1n4001]
  D3 = Diode [package=diode-1n4001]
  D5 = Diode [package=diode-1n4001]
  D7 = Diode [package=diode-1n4001]
  D2 = Diode [package=diode-1n4001]
  D9 = Diode [package=diode-1n4001]
  D10 = Diode [package=diode-1n4001]
  VR1 = Potentiometer [package="DIP [THT]"]
  J23 = Audio Jack 3.5mm [part_number=3.5mm package="[THT]"]
  J24 = Audio Jack 3.5mm [part_number=3.5mm package="[THT]"]
  J25 = Audio Jack 3.5mm [part_number=3.5mm package="[THT]"]
  J26 = Audio Jack 3.5mm [part_number=3.5mm package="[THT]"]
  VR2 = Trimpot-3296 [package=3386u]
  VR1_2 = Trimpot-3296 [package=3386u]
  Power_plug1 = Power plug

nets (from the breadboard view):
  N1: J15.pin1, J15.pin2, R5.Pin_1
  N2: J11.pin1, J10.pin1, R1.Pin_1, R4.Pin_1, R2.Pin_1, J9.pin1, R3.Pin_1, J12.pin1, D4.C, D6.C, D8.C, D2.C, VR1.B2
  GND: J11.pin2, J10.pin2, C1.-, R6.Pin_0, J7.pin9, J1.pin8, J9.pin2, J6.pin9, R8.Pin_1, C2.-, J5.pin9, J2.pin8, J3.pin8, RCA1.SHELL, RCA2.SHELL, U2.connector3, J4.pin8, J8.pin9, J12.pin2, D1.A, D3.A, D5.A, D7.A, D9.A, D10.A, VR1.A1, J23.GND, J24.GND, J25.GND, J26.GND, Power_plug1.GND
  N3: R5.Pin_0, J21.pin1, J21.pin2, C2.+, U2.connector4
  N4: J14.pin1, J14.pin2, R6_2.Pin_1
  N5: R1.Pin_0, J23.Ring_1
  N6: J19.pin1, J26.Tip_2
  N7: J19.pin2, D8.A, D7.C, J26.Tip_1
  N8: C1.+, R6_2.Pin_0, J22.pin1, J22.pin2, U2.connector2
  N9: Fuse1.Connector1, Power_plug1.VCC
  N10: Fuse1.Connector2, Q2.collector, Q1.collector, U2.connector7
  N11: R6.Pin_1, U2.connector1, VR1_2.WIPER
  N12: R4.Pin_0, J26.Ring_1
  N13: Q2.base, U2.connector6, VR2.CCW
  N14: Q2.emitter, RCA2.PIN, D10.C
  N15: R2.Pin_0, J24.Ring_1
  N16: J18.pin1, J25.Tip_2
  N17: J18.pin2, D6.A, D5.C, J25.Tip_1
  N18: J7.pin1, J6.pin1, J5.pin1, J8.pin1
  N19: J7.pin2, J6.pin2, J5.pin2, J8.pin2
  N20: J7.pin3, J6.pin3, J5.pin3, J8.pin3
  N21: J7.pin4, J6.pin4, J5.pin4, J8.pin4
  N22: J7.pin5, J6.pin5, J5.pin5, J8.pin5
  N23: J7.pin6, J6.pin6, J5.pin6, J8.pin6
  N24: J7.pin7, J6.pin7, J5.pin7, J8.pin7
  N25: J7.pin8, J6.pin8, J5.pin8, J8.pin8
  N26: J1.pin1, J2.pin1, J3.pin1, J4.pin1
  N27: J1.pin2, J2.pin2, J3.pin2, J4.pin2
  N28: J1.pin3, J2.pin3, J3.pin3, J4.pin3
  N29: J1.pin4, J2.pin4, J3.pin4, J4.pin4
  N30: J1.pin5, J2.pin5, J3.pin5, J4.pin5
  N31: J1.pin6, J2.pin6, J3.pin6, J4.pin6
  N32: J1.pin7, J2.pin7, J3.pin7, J4.pin7
  N33: J17.pin1, J24.Tip_2
  N34: J17.pin2, D4.A, D3.C, J24.Tip_1
  N35: J16.pin1, J23.Tip_2
  N36: J16.pin2, D1.C, D2.A, J23.Tip_1
  N37: Q1.base, U2.connector0, VR1_2.CCW
  N38: Q1.emitter, RCA1.PIN, D9.C
  N39: R8.Pin_0, U2.connector5, VR2.WIPER
  N40: R3.Pin_0, J25.Ring_1
  N41: J13.pin1, J13.pin2, VR1.SW2
  N42: VR1.Wiper, VR1.SW1

custom parts:
  Potentiometer: Potentiometer with switch
  Audio Jack 3.5mm: Audio Jack Mono/Stereo 3.5mm
  Trimpot-3296: Trimpot 3296 / 25 turn stand
  Power plug: power plug
